// Logisim project processor.circ as structural Verilog: 8 circuits, main circuit main
module main (
  input  [7:0] jump_address,
  input  jump,
  input  [7:0] branch_address,
  input  branch,
  input  Enable,
  input  Clear,
  output [7:0] out_7,
  output [7:0] out_8
);

  wire Clock_out;
  wire [7:0] multiplexer_2_out, program_counter_1_pc;

  Clock Clock (.out(Clock_out));
  Program_Counter program_counter_1 (
    .In(multiplexer_2_out), .Clock(Clock_out), .Clear(Clear), .PC(program_counter_1_pc));
  Instruction_Memory instruction_memory_1 (
    .Address(program_counter_1_pc), .Enable(Enable));  // open: out_3, out_4, out_5, out_6, Instruction
  Adder adder_1 (.a(program_counter_1_pc), .b(8'h1), .out(out_8), .cin(1'b0));  // open: cout
  Control_Unit control_unit_1 ();  // open: Opcode, Enable, Shift_Right, Shift_Left, Cin, s0, s1, s2, MemWrite, MemRead, Jump, Branch_Not_Equal, Branch_Equal, RegWrite, MemToReg, ALUSrc, RegDst
  Register_File register_file_1 ();  // open: RegWrite, Reg1, Reg2, WriteReg, Data, Clock, Clear, Read_1, Read_2
  Multiplexer #(.width(8)) multiplexer_1 (.in0(out_8), .in1(branch_address), .out(out_7), .sel(branch), .en(1'b1));
  ALU alu_1 ();  // open: Cin, A, B, S, s2, s1, s0
  Data_Memory data_memory_1 ();  // open: Address, Data, MemWrite, Clock, MemRead, Clear, Out
  Multiplexer #(.width(8)) multiplexer_2 (
    .in0(out_7), .in1(jump_address), .out(multiplexer_2_out), .sel(jump), .en(1'b1));

  // Notes on the sheet:
  //   PC+1
endmodule

// PC
module Program_Counter (
  input  [7:0] In,
  input  Clock,
  input  Clear,
  output [7:0] PC
);

  Register register_1 (.D(In), .en(1'b1), .Q(PC), .clk(Clock), .clr(Clear));
endmodule

// IM
module Instruction_Memory (
  input  [7:0] Address,
  input  Enable,
  output [3:0] out_3,
  output [3:0] out_4,
  output [3:0] out_5,
  output [3:0] out_6,
  output [15:0] Instruction
);

  ROM #(.dataWidth(16)) rom_1 (.addr(Address), .data(Instruction), .sel(Enable));

  assign out_3 = Instruction[3:0];
  assign out_4 = Instruction[7:4];
  assign out_5 = Instruction[11:8];
  assign out_6 = Instruction[15:12];

  // Notes on the sheet:
  //   contents of rom_1 (hex, n*v repeats v):
  //   104
endmodule

// RF
module Register_File (
  input  RegWrite,
  input  [3:0] Reg1,
  input  [3:0] Reg2,
  input  [3:0] WriteReg,
  input  [3:0] Data,
  input  Clock,
  input  Clear,
  output [3:0] Read_1,
  output [3:0] Read_2
);

  wire and_1_out, and_2_out, and_3_out, and_4_out, and_5_out, and_6_out, and_7_out, and_8_out,
       decoder_1_out0, decoder_1_out1, decoder_1_out2, decoder_1_out3, decoder_1_out4, decoder_1_out5,
       decoder_1_out6, decoder_1_out7;
  wire [3:0] register_1_q, register_2_q, t0_q, t1_q, t2_q, t3_q, t4_q, Zero_q;

  Decoder #(.select(3)) decoder_1 (
    .out0(decoder_1_out0), .out1(decoder_1_out1), .out2(decoder_1_out2), .out3(decoder_1_out3),
    .out4(decoder_1_out4), .out5(decoder_1_out5), .out6(decoder_1_out6), .out7(decoder_1_out7),
    .sel(WriteReg[2:0]), .en(1'b1));
  and and_1 (and_1_out, RegWrite, decoder_1_out0);
  and and_2 (and_2_out, RegWrite, decoder_1_out1);
  and and_3 (and_3_out, RegWrite, decoder_1_out2);
  and and_4 (and_4_out, RegWrite, decoder_1_out3);
  and and_5 (and_5_out, RegWrite, decoder_1_out4);
  and and_6 (and_6_out, RegWrite, decoder_1_out5);
  and and_7 (and_7_out, RegWrite, decoder_1_out6);
  and and_8 (and_8_out, RegWrite, decoder_1_out7);
  Register #(.width(4)) Zero (.D(4'b0000), .en(and_1_out), .Q(Zero_q), .clk(Clock), .clr(Clear));
  Register #(.width(4)) t0 (.D(Data), .en(and_2_out), .Q(t0_q), .clk(Clock), .clr(Clear));
  Register #(.width(4)) t1 (.D(Data), .en(and_3_out), .Q(t1_q), .clk(Clock), .clr(Clear));
  Register #(.width(4)) t2 (.D(Data), .en(and_4_out), .Q(t2_q), .clk(Clock), .clr(Clear));
  Register #(.width(4)) t3 (.D(Data), .en(and_5_out), .Q(t3_q), .clk(Clock), .clr(Clear));
  Register #(.width(4)) t4 (.D(Data), .en(and_6_out), .Q(t4_q), .clk(Clock), .clr(Clear));
  Register #(.width(4)) register_1 (.D(Data), .en(and_7_out), .Q(register_1_q), .clk(Clock), .clr(Clear));
  Register #(.width(4)) register_2 (.D(Data), .en(and_8_out), .Q(register_2_q), .clk(Clock), .clr(Clear));
  Multiplexer #(.select(3), .width(4)) multiplexer_1 (
    .in0(Zero_q), .in1(t0_q), .in2(t1_q), .in3(t2_q), .in4(t3_q), .in5(t4_q), .in6(register_1_q),
    .in7(register_2_q), .out(Read_1), .sel(Reg1[2:0]), .en(1'b1));
  Multiplexer #(.select(3), .width(4)) multiplexer_2 (
    .in0(Zero_q), .in1(t0_q), .in2(t1_q), .in3(t2_q), .in4(t3_q), .in5(t4_q), .in6(register_1_q),
    .in7(register_2_q), .out(Read_2), .sel(Reg2[2:0]), .en(1'b1));
endmodule

// DM
module Data_Memory (
  input  [7:0] Address,
  input  [3:0] Data,
  input  MemWrite,
  input  Clock,
  input  MemRead,
  input  Clear,
  output [3:0] Out
);

  RAM #(.dataWidth(4), .bus("separate")) ram_1 (
    .addr(Address), .din(Data), .data(Out), .str(MemWrite), .sel(1'b1), .clk(Clock), .ld(MemRead), .clr(Clear));
endmodule

module ALU (
  input  Cin,
  input  s2,
  input  s1,
  input  s0,
  input  [3:0] A,
  input  [3:0] B,
  output [3:0] S
);

  wire adder_1_cout, adder_2_cout, adder_3_cout, alu_adder_module_1_xi, alu_adder_module_1_yi,
       alu_adder_module_1_zi, alu_adder_module_2_xi, alu_adder_module_2_yi, alu_adder_module_2_zi,
       alu_adder_module_3_xi, alu_adder_module_3_yi, alu_adder_module_3_zi, alu_adder_module_4_xi,
       alu_adder_module_4_yi, alu_adder_module_4_zi;

  ALU_Adder_Module alu_adder_module_1 (
    .s2(s2), .s1(s1), .s0(s0), .Ai(A[0]), .Bi(B[0]), .Ci(Cin), .Xi(alu_adder_module_1_xi),
    .Yi(alu_adder_module_1_yi), .Zi(alu_adder_module_1_zi));
  ALU_Adder_Module alu_adder_module_2 (
    .s2(s2), .s1(s1), .s0(s0), .Ai(A[1]), .Bi(B[1]), .Ci(adder_1_cout), .Xi(alu_adder_module_2_xi),
    .Yi(alu_adder_module_2_yi), .Zi(alu_adder_module_2_zi));
  ALU_Adder_Module alu_adder_module_3 (
    .s2(s2), .s1(s1), .s0(s0), .Ai(A[2]), .Bi(B[2]), .Ci(adder_2_cout), .Xi(alu_adder_module_3_xi),
    .Yi(alu_adder_module_3_yi), .Zi(alu_adder_module_3_zi));
  ALU_Adder_Module alu_adder_module_4 (
    .s2(s2), .s1(s1), .s0(s0), .Ai(A[3]), .Bi(B[3]), .Ci(adder_3_cout), .Xi(alu_adder_module_4_xi),
    .Yi(alu_adder_module_4_yi), .Zi(alu_adder_module_4_zi));
  Adder #(.width(1)) adder_1 (
    .a(alu_adder_module_1_xi), .b(alu_adder_module_1_yi), .out(S[0]), .cin(alu_adder_module_1_zi),
    .cout(adder_1_cout));
  Adder #(.width(1)) adder_2 (
    .a(alu_adder_module_2_xi), .b(alu_adder_module_2_yi), .out(S[1]), .cin(alu_adder_module_2_zi),
    .cout(adder_2_cout));
  Adder #(.width(1)) adder_3 (
    .a(alu_adder_module_3_xi), .b(alu_adder_module_3_yi), .out(S[2]), .cin(alu_adder_module_3_zi),
    .cout(adder_3_cout));
  Adder #(.width(1)) adder_4 (
    .a(alu_adder_module_4_xi), .b(alu_adder_module_4_yi), .out(S[3]), .cin(alu_adder_module_4_zi));  // open: cout

  // Notes on the sheet:
  //   A0
  //   B0
  //   A1
  //   A2
  //   B2
  //   A3
  //   B3
  //   S0
  //   S1
  //   S2
  //   S3
endmodule

// Add_Module
module ALU_Adder_Module (
  input  s2,
  input  s1,
  input  s0,
  input  Ai,
  input  Bi,
  input  Ci,
  output Xi,
  output Yi,
  output Zi
);

  wire and_1_out, and_2_out, and_4_out, and_5_out, and_6_out, not_1_out, not_2_out, not_3_out, or_1_out,
       xor_1_out;

  not not_1 (not_1_out, s2);
  not not_2 (not_2_out, s1);
  not not_3 (not_3_out, Bi);
  and and_1 (and_1_out, s1, Bi);
  and and_2 (and_2_out, s0, not_2_out, not_3_out);
  or or_1 (or_1_out, and_1_out, and_2_out);
  xor xor_1 (xor_1_out, s0, Bi);
  and and_3 (Zi, Ci, not_1_out);
  and and_4 (and_4_out, or_1_out, s2);
  and and_5 (and_5_out, xor_1_out, not_2_out);
  and and_6 (and_6_out, s1, s0);
  or or_2 (Xi, and_4_out, Ai);
  or or_3 (Yi, and_5_out, and_6_out);
endmodule

module Control_Unit (
  input  [3:0] Opcode,
  input  Enable,
  output Shift_Right,
  output Shift_Left,
  output Cin,
  output s0,
  output s1,
  output s2,
  output MemWrite,
  output MemRead,
  output Jump,
  output Branch_Not_Equal,
  output Branch_Equal,
  output RegWrite,
  output MemToReg,
  output ALUSrc,
  output RegDst
);

  wire [0:0] rom_1_data;

  ROM #(.addrWidth(4), .dataWidth(16)) rom_1 (
    .addr(Opcode),
    .data({RegDst, ALUSrc, MemToReg, RegWrite, Branch_Equal, Branch_Not_Equal, Jump, MemRead, MemWrite, s2, s1, s0, Cin, Shift_Left, Shift_Right, rom_1_data[0]}),
    .sel(Enable));

  // Notes on the sheet:
  //   contents of rom_1 (hex, n*v repeats v):
  //   9018 5004 4080 5000 7100 9050 5060 5018 9000 9060 418 5002 200 9070 5050 818
endmodule
